# Fritzing sketch Seatalk 1 Breadboard sch-v1 (saved by Fritzing 0.9.3b)
breadboards: 2

parts:
  R1 = Resistor [tolerance=±5% power=0.25 resistance=4.7k package=THT]
  R2 = Resistor [tolerance=±5% power=0.25 resistance=39k package=THT]
  R3 = Resistor [tolerance=±5% power=0.25 resistance=15k package=THT]
  R4 = Resistor [tolerance=±5% power=0.25 resistance=27k package=THT]
  R5 = Resistor [tolerance=±5% power=0.25 resistance=6.8k package=THT]
  R6 = Resistor [tolerance=±5% power=0.25 resistance=1k package=THT]
  R7 = Resistor [tolerance=±5% power=0.25 resistance=1k package=THT]
  R8 = Resistor [tolerance=±5% power=0.25 resistance=10 package=THT]
  D1 = Rectifier Diode [part_number=1N4148 mpn=1N4148 package="300 mil [THT]"]
  R9 = Resistor [tolerance=±5% power=0.25 resistance=390 package=THT]
  R10 = Resistor [tolerance=±5% power=0.25 resistance=39k package=THT]
  R11 = Resistor [tolerance=±5% power=0.25 resistance=2.2k package=THT]
  R12 = Resistor [tolerance=±5% power=0.25 resistance=2.2k package=THT]
  R13 = Resistor [tolerance=±5% power=0.25 resistance=10k package=THT]
  C1 = Ceramic Capacitor [capacitance=100nF voltage=35V package="100 mil [THT, multilayer]"]
  R15 = Resistor [tolerance=±5% power=0.25 resistance=2.2k package=THT]
  R16 = Resistor [tolerance=±5% power=0.25 resistance=2.2k package=THT]
  R17 = Resistor [tolerance=±5% power=0.25 resistance=4.7k package=THT]
  D2 = Rectifier Diode [part_number=1N4148 mpn=1N4148 package="300 mil [THT]"]
  L1 = Inductor [inductance=1µH package="400 mil [THT]"]
  L2 = Inductor [inductance=10µH package="400 mil [THT]"]
  C2 = Ceramic Capacitor [capacitance=1pF voltage=35V package="100 mil [THT, multilayer]"]
  L3 = Inductor [inductance=10µH package="400 mil [THT]"]
  L4 = Inductor [inductance=10µH package="400 mil [THT]"]
  C3 = Ceramic Capacitor [capacitance=1µF voltage=35V package="100 mil [THT, multilayer]"]
  C4 = Ceramic Capacitor [capacitance=1µF voltage=35V package="100 mil [THT, multilayer]"]
  D3 = Rectifier Diode [part_number=1N4001 mpn=1N4001 package="300 mil [THT]"]
  C5 = Electrolytic Capacitor [capacitance=330µF voltage=35V package="100 mil [THT, electrolytic]"]
  D4 = Rectifier Diode [part_number=1N4001 mpn=1N4001 package="300 mil [THT]"]
  R18 = Resistor [tolerance=±5% power=0.25 resistance=10 package=THT]
  R19 = Resistor [tolerance=±5% power=0.25 resistance=10 package=THT]
  C6 = Electrolytic Capacitor [capacitance=220µF voltage=35V package="100 mil [THT, electrolytic]"]
  U1 = Voltage Regulator - 5V [mpn=7805 package="TO220 [THT]"]
  M1 = DOIT Esp32 DevKit v1 (30 pins long, 11 pins width) [part_number=ESP32S-PIN30]
  Q1 = NPN-Transistor [mpn=BC548 package="TO92 [THT]"]
  Q2 = NPN-Transistor [mpn=BC548 package="TO92 [THT]"]
  Q3 = NPN-Transistor [mpn=BC548 package="TO92 [THT]"]
  Q5 = PNP-Transistor [mpn=BC558 package="TO92 [THT]"]
  Q4 = NPN-Transistor [mpn=BC548 package="TO92 [THT]"]
  Q6 = NPN-Transistor [mpn=BC548 package="TO92 [THT]"]
  R14 = Resistor [tolerance=±5% power=0.25 resistance=220 package=THT]
  JTAG_Debug = Header 5x2 [mn=Espresive mpn=ESP-Prog package=avr_icsp]
  LCD1 = 2.8" SPI TFT Module [part_number=MSP2807]
  D5 = Rectifier Diode [part_number=1N4001 mpn=1N4001 package="300 mil [THT]"]
  R25 = Resistor [tolerance=±5% power=0.25 resistance=220 package=THT]
  Q8 = PNP-Transistor [mpn=BC558 part_number=/7 package="TO92 [THT]"]
  R26 = Resistor [tolerance=±5% power=0.25 resistance=10k package=THT]
  Q9 = NPN-Transistor [mpn=BC548 package="TO92 [THT]"]
  R27 = Resistor [tolerance=±5% power=0.25 resistance=1k package=THT]
  SG1 = Buzzer 12mm [part_number=Buzzer package=buzzer-12mm]
  Q10 = NPN-Transistor [mpn=BC548 package="TO92 [THT]"]
  R28 = Resistor [tolerance=±5% power=0.25 resistance=4.7k package=THT]
  R29 = Resistor [tolerance=±5% power=0.25 resistance=10k package=THT]

nets:
  GND: R1.Pin_0, R8.Pin_0, C2.0, L4.pin_1, C4.0, C5.-, C6.-, U1.GND, M1.GND, Q1.E, Q2.E, Q4.E, Q6.E, JTAG_Debug.3, JTAG_Debug.5, JTAG_Debug.7, JTAG_Debug.9, LCD1.pin2, Q9.E, Q10.E
  N1: R1.Pin_1, R2.Pin_0, Q1.B
  N2: R2.Pin_1, R3.Pin_0, D2.anode
  12V: R3.Pin_1, R10.Pin_1, R12.Pin_1, D4.cathode, Q5.E, R14.Pin_1
  N3: R4.Pin_0, Q1.C, Q2.B
  3.3V: R4.Pin_1, R5.Pin_1, R11.Pin_1, R17.Pin_1, M1.3V3, JTAG_Debug.1, SG1.2
  N4: R5.Pin_0, R6.Pin_0, Q2.C
  RXD: R6.Pin_1, M1.D25, M1.D26
  N5: R7.Pin_0, R8.Pin_1, Q3.E
  N6: R7.Pin_1, R16.Pin_0, Q4.B
  N7: D1.cathode, Q3.C
  N8: D1.anode, R9.Pin_0, D2.cathode, L2.pin_1
  N9: R9.Pin_1, R10.Pin_0, Q5.C
  N10: R11.Pin_0, Q3.B, Q4.C
  N11: R12.Pin_0, R13.Pin_1, Q5.B
  N12: R13.Pin_0, C1.1
  N13: C1.0, Q6.C, R14.Pin_0
  N14: R15.Pin_0, Q6.B
  TXD: R15.Pin_1, R16.Pin_1, R17.Pin_0, M1.D27
  Seatalk: L1.pin_0
  N15: L1.pin_1, L2.pin_0, C2.1
  ST12V: L3.pin_0, C3.1
  N16: L3.pin_1, C4.1, D3.anode, D4.anode
  ST0V: L4.pin_0, C3.0
  N17: D3.cathode, R18.Pin_1, R19.Pin_1
  N18: C5.+, R18.Pin_0, R19.Pin_0, U1.input_voltage
  N19: C6.+, U1.output_voltage, D5.anode
  N20: M1.D15, JTAG_Debug.6
  N21: M1.D4, R27.Pin_1
  N22: M1.TX2, LCD1.pin4
  N23: M1.D5, LCD1.pin11
  N24: M1.D18, LCD1.pin7, LCD1.pin10
  N25: M1.D19, LCD1.pin9, LCD1.pin13
  N26: M1.D21, LCD1.pin5
  N27: M1.TX0, R29.Pin_0
  N28: M1.D22, LCD1.pin3
  N29: M1.D23, LCD1.pin6, LCD1.pin12
  N30: M1.D14, JTAG_Debug.2
  N31: M1.D12, JTAG_Debug.8
  N32: M1.D13, JTAG_Debug.4
  5V: M1.VIN, LCD1.pin1, D5.cathode, Q8.E, R28.Pin_1
  N33: LCD1.pin8, R25.Pin_1
  N34: R25.Pin_0, Q8.C
  N35: Q8.B, R26.Pin_0
  N36: R26.Pin_1, Q10.C, R28.Pin_0
  N37: Q9.B, R27.Pin_0
  N38: Q9.C, SG1.1
  N39: Q10.B, R29.Pin_1

notes:
  Raymarine Seatalk 1
  Seatalk TX
  Debug
  1 - 3v3
  3,5,7,9 - GND
  2 - TMS
  4 - TCK
  6 - TDO
  8 - TDI
  10 - N/C
  Seatalk RX
  User Interface
  Power

custom parts:
  DOIT Esp32 DevKit v1 (30 pins long, 11 pins width): The DOIT Esp32 DevKit v1 is one of the development board created by DOIT to evaluate the ESP-WROOM-32 module. It is based on the ESP32 microcontroller that boasts Wifi, Bluetooth, Ethernet and Low Power support all in a single chip. (vanepp) made breadboard work, adjusted pin numbering and labels and reduced size of schematic and cleaned up pcb. This chip is 30pins long (2 x15) and 11 pins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
  2.8" SPI TFT Module: A generic 2.8 inch LCD TFT 320x240 display with touchscreen and SD card slot. Uses the ILI9341 controller, like the Adafruit displays of this size uses.
